// Logisim project not_gate.circ as structural Verilog
module main (
  input  a,
  output y
);

  wire not_gate_1_y;

  not_gate not_gate_1 (.a(a), .y(not_gate_1_y));

  // Notes on the sheet:
  //   a: initial=0xffffffff
endmodule

// VHDL entity not_gate, as the project stores it:
library ieee;
use ieee.std_logic_1164.all;

entity not_gate is
    port (
        a : in std_logic;
        y : out std_logic
    );
end entity not_gate;

architecture behavioral of not_gate is
begin
    y <= not a;
end architecture behavioral;
